# Fritzing sketch Diagram_RoboCar_Bluetooth_2023 (saved by Fritzing 0.9.3b)

parts:
  Part2 = Bluetooth HC-05 Macho
  Part3 = Arduino Nano (Rev3.0)
  L298N1 = L298N DC motor driver
  M1 = DC Motor
  M2 = DC Motor
  M3 = DC Motor
  M4 = DC Motor
  U1 = LM2596 step down module
  U2 = LM2596 step down module
  Power_plug1 = Power plug
  J1 = Basic Servo
  J2 = Basic Servo
  J3 = Basic Servo
  C1 = Capacitor [package=cap-pth-small2]
  C2 = Capacitor [package=cap-pth-small2]
  U3 = SWITCH_SPDT [package=kps-1290]

nets:
  N1: Part2.TXD, Part3.D2
  VCC: Part2.VCC, Part3.5V
  GND: Part3.GND, L298N1.GND, U1.IN-, U1.OUT-, U2.IN-, U2.OUT-, Power_plug1.GND, J1.gnd, J2.gnd, C1.2, C2.2
  N2: Part3.D3, J1.pulse
  N3: Part3.D6, J2.pulse
  N4: Part3.D9, J3.pulse
  N5: Part3.VIN, U2.OUT+, C2.1
  N6: Part3.A5, L298N1.IN3
  N7: Part3.A4, L298N1.IN4
  N8: Part3.A3, L298N1.ENB
  N9: Part3.A2, L298N1.ENA
  N10: Part3.A1, L298N1.IN2
  N11: Part3.A0, L298N1.IN1
  N12: L298N1.OUT1, M1.pin_1, M2.pin_1
  N13: L298N1.OUT2, M1.pin_2, M2.pin_2
  N14: L298N1.OUT3, M3.pin_1, M4.pin_1
  N15: L298N1.OUT4, M3.pin_2, M4.pin_2
  N16: L298N1.12V, U1.IN+, U2.IN+, U3.P
  VCC_2: U1.OUT+, J1.vcc, J2.vcc, J3.vcc, C1.1
  N17: Power_plug1.VCC, U3.O

notes:
  Module Bluetooth HC-05
  Arduino --- Bluetooth
  2 TX
  Mạch Giảm Áp DC LM2596 3A
  Điện áp đầu vào: Từ 3V-30V.
  Điện áp đầu ra: Điều chỉnh 1.5V-30V.
  Dòng tối đa: 3A.
  Hiệu suất: 92%
  Công suất: 15W
  Module L298N
  Arduino --- L298N
  ENA A2
  IN_1 A0
  IN_2 A1
  IN_3 A5
  IN_4 A4
  ENB A3
  Servo SG90
  Arduino --- Servo
  6 S1
  3 S2
  9 S3
  OUT: 5V
  Battery18650x3
  Power Supply = 12V
  IN: 12V
  S1
  S2
  S3

custom parts:
  L298N DC motor driver: 2x DC motor driver with 78M05 positive voltage regulator (7..35 V) L298N: max 46 V, 2 A Set 5 V Enable jumper to enable 5 V regultor (needed for the L298N) and +5 V output at screw terminal or supply external +5 V at screw terminal Set ENA and/or ENB to +5 V to enable motor permanently or supply ENA and/or ENB with PWM signal IN1 and IN2 set rotation directory for motor A (OUT1/OUT2) IN2 and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
  LM2596 step down module: LM2596 DC-DC step down power supply module 3 A.

// code stored in the sketch: l298n hc05.ino
#include <Arduino.h>
#include <Wire.h>
#include <SoftwareSerial.h>

double angle_rad = PI/180.0;
double angle_deg = 180.0/PI;
void Left_Motor_Forwards();
double IN1;
double IN2;
double IN3;
double IN4;
void Right_Motor_Forwards();
void Left_Motor_Forwards_Right_Motor_Backwards();
void BOTH_Motors_Forward();
void BOTH_Motors_OFF();
void BOTH_Motors_Backward();
void Left_Motor_Backwards_Right_Motor_Forwards();
void Right_Motor_Backwards();
void Left_Motor_Backwards();
SoftwareSerial Bluetooth(0, 1);
char Data;
void sendData(String transmitData){
Bluetooth.println(transmitData);}

void Left_Motor_Forwards()
{
    digitalWrite(IN1,0);
    digitalWrite(IN2,0);
    digitalWrite(IN3,0);
    digitalWrite(IN4,1);
}

void Right_Motor_Forwards()
{
    digitalWrite(IN1,0);
    digitalWrite(IN2,1);
    digitalWrite(IN3,0);
    digitalWrite(IN4,0);
}

void Left_Motor_Forwards_Right_Motor_Backwards()
{
    digitalWrite(IN1,1);
    digitalWrite(IN2,0);
    digitalWrite(IN3,0);
    digitalWrite(IN4,1);
}

void BOTH_Motors_Forward()
{
    digitalWrite(IN1,0);
    digitalWrite(IN2,1);
    digitalWrite(IN3,0);
    digitalWrite(IN4,1);
}

void BOTH_Motors_OFF()
{
    digitalWrite(IN1,0);
    digitalWrite(IN2,0);
    digitalWrite(IN3,0);
    digitalWrite(IN4,0);
}

void BOTH_Motors_Backward()
{
    digitalWrite(IN1,1);
    digitalWrite(IN2,0);
    digitalWrite(IN3,1);
    digitalWrite(IN4,0);
}

void Left_Motor_Backwards_Right_Motor_Forwards()
{
    digitalWrite(IN1,0);
    digitalWrite(IN2,1);
    digitalWrite(IN3,1);
    digitalWrite(IN4,0);
}

void Right_Motor_Backwards()
{
    digitalWrite(IN1,1);
    digitalWrite(IN2,0);
    digitalWrite(IN3,0);
    digitalWrite(IN4,0);
}

void Left_Motor_Backwards()
{
    digitalWrite(IN1,0);
    digitalWrite(IN2,0);
    digitalWrite(IN3,1);
    digitalWrite(IN4,0);
}

void setup(){
    Bluetooth.begin(9600);
    IN1 = 7;
    IN2 = 6;
    IN3 = 5;
    IN4 = 4;
    pinMode(IN1,OUTPUT);
    pinMode(IN2,OUTPUT);
    pinMode(IN3,OUTPUT);
    pinMode(IN4,OUTPUT);
}

void loop(){
    if(Bluetooth.available()){
        Data=Bluetooth.read();
        if(Data==('1')){
            sendData("L forward");
            Left_Motor_Forwards();
        }
        if(Data==('2')){
            sendData("L backward");
            Left_Motor_Backwards();
        }
        if(Data==('3')){
            sendData("R forward");
            Right_Motor_Forwards();
        }
        if(Data==('4')){
            sendData("R backward");
            Right_Motor_Backwards();
        }
        if(Data==('5')){
            sendData("L forward R backward");
            Left_Motor_Forwards_Right_Motor_Backwards();
        }
        if(Data==('6')){
            sendData("L backward R forward");
            Left_Motor_Backwards_Right_Motor_Forwards();
        }
        if(Data==('7')){
            sendData("L&R forward");
            BOTH_Motors_Forward();
        }
        if(Data==('8')){
            sendData("L&R backward");
            BOTH_Motors_Backward();
        }
        if(Data==('0')){
            sendData("L&R OFF");
            BOTH_Motors_OFF();
        }
    }
    _loop();
}

void _delay(float seconds){
    long endTime = millis() + seconds * 1000;
    while(millis() < endTime)_loop();
}

void _loop(){
}
